// Logisim project Questao1_b.circ as structural Verilog: 1 circuit, main circuit main
module main (
  input  A,
  input  B,
  output X
);

  wire nand_1_out;

  nand nand_1 (nand_1_out, A, B);
  not not_1 (X, nand_1_out);
endmodule
