// Logisim project Questao1_d.circ as structural Verilog: 1 circuit, main circuit main
module main (
  input  A,
  input  B,
  output X
);

  wire and_1_out;

  not not_1 (X, and_1_out);
  and and_1 (and_1_out, A, B);
endmodule
