// Logisim project Quetsao1_a.circ as structural Verilog: 1 circuit, main circuit main
module main (
  input  A,
  output X
);

  wire not_1_out;

  not not_1 (not_1_out, A);
  not not_2 (X, not_1_out);
endmodule
